# Fritzing sketch circuitDiagram (saved by Fritzing 0.9.3b)

parts:
  Raspberry_Pi_1 = Raspberry Pi 3 [part_number=RPI-3-V1.2]
  Front_Right_Motor = DC Motor
  Front_Left_Motor = DC Motor
  Back_Left_Motor = DC Motor
  Back_Right_Motor = DC Motor
  Front_Right_Relay = RELAY [package=OJ]
  Back_Left_Relay = RELAY [package=OJ]
  Back_Right_Relay = RELAY [package=OJ]
  Front_Left_Relay = RELAY [package=OJ]
  Motor_Power = Battery Holders [package=lipo-1100mAh]
  hc-sr1 = hc-sr04

nets:
  3V3: Raspberry_Pi_1.3v3, Raspberry_Pi_1.3V3, hc-sr1.VCC
  N1: Raspberry_Pi_1.GPIO4, hc-sr1.Trig
  N2: Raspberry_Pi_1.GPIO17, hc-sr1.Echo
  GND: Raspberry_Pi_1.GND, Front_Right_Relay.COIL1, Back_Left_Relay.COIL1, Back_Right_Relay.COIL1, Front_Left_Relay.COIL1, hc-sr1.GND
  N3: Raspberry_Pi_1.GPIO21, Front_Left_Relay.COIL2
  N4: Raspberry_Pi_1.GPIO20, Front_Right_Relay.COIL2
  N5: Raspberry_Pi_1.GPIO16, Back_Left_Relay.COIL2
  N6: Raspberry_Pi_1.GPIO12, Back_Right_Relay.COIL2
  N7: Front_Right_Motor.pin_1, Front_Right_Relay.MAIN
  N8: Front_Right_Motor.pin_2, Front_Left_Motor.pin_2, Back_Left_Motor.pin_2, Back_Right_Motor.pin_2, Motor_Power.-
  N9: Front_Left_Motor.pin_1, Front_Left_Relay.MAIN
  N10: Back_Left_Motor.pin_1, Back_Left_Relay.MAIN
  N11: Back_Right_Motor.pin_1, Back_Right_Relay.MAIN
  N12: Front_Right_Relay.NO, Back_Left_Relay.NO, Motor_Power.+
  N13: Back_Right_Relay.NO, Front_Left_Relay.NO

custom parts:
  hc-sr04: This is a HC-SR04 Distance Sensor
